# Fritzing sketch CapacityMonitorDiagramSimple (saved by Fritzing 0.9.3b)
circuit board: 8.46667cm x 5.64444cm
breadboards: 1

parts:
  IC1 = L293D [package=THT]
  Part1 = Arduino Pro Mini (3.3V)
  R1 = Resistor [tolerance=±5% resistance=1k package=THT]
  R2 = Resistor [tolerance=±5% resistance=10k package=THT]
  R3 = Resistor [tolerance=±5% resistance=1 package=THT]
  L1 = Inductor [package="0805 [SMD]"]
  U2 = POT [package=pot_mammoth]
  L2 = Inductor [package="400 mil [THT]"]

nets:
  N1: IC1.Enable_1, Part1.SCK
  N2: IC1.In_1, Part1.D3
  N3: IC1.Out_1_(_Controlled_by_Enable_1_), L1.pin_0
  N4: IC1.0V, Part1.GND, R2.Pin_0, U2.A, L2.pin_0
  N5: IC1.Out_2_(_Controlled_by_Enable_1_), R3.Pin_0
  N6: IC1.In_2, Part1.D4
  N7: IC1.+Vmotor, IC1.+V, Part1.VCC, L2.pin_1
  N8: Part1.A0, R2.Pin_1, U2.S
  N9: Part1.MOSI, R1.Pin_0
  N10: R1.Pin_1, U2.E
  N11: R3.Pin_1, L1.pin_1
